# Fritzing sketch board (saved by Fritzing 0.9.4)
breadboards: 1

parts:
  LED1 = LED - 5mm [color="Red (633nm)" package="5 mm [THT]"]
  LED2 = LED - 5mm [color="Green (555nm)" package="5 mm [THT]"]
  S1 = Pushbutton [package="[THT]"]
  S2 = Pushbutton [package="[THT]"]
  R1 = Resistor [tolerance=±5% resistance=10k package="0603 [SMD]"]
  R2 = Resistor [tolerance=±5% resistance=10k package="0603 [SMD]"]
  R3 = Resistor [tolerance=±5% resistance=220 package="0603 [SMD]"]
  R4 = Resistor [tolerance=±5% resistance=220 package="0603 [SMD]"]
  Part1 = Arduino Uno (Rev3)

nets:
  N1: LED1.cathode, LED2.cathode, R1.Pin_1, R2.Pin_1, Part1.GND
  N2: LED1.anode, R4.Pin_0
  N3: LED2.anode, R3.Pin_0
  N4: S1.Pin_1, S1.Pin_2, R2.Pin_0, Part1.D8
  N5: S1.Pin_3, S1.Pin_4, S2.Pin_3, S2.Pin_4, Part1.5V
  N6: S2.Pin_1, S2.Pin_2, R1.Pin_0, Part1.D2
  N7: R3.Pin_1, Part1.D4
  N8: R4.Pin_1, Part1.D12/MISO

notes:
  Unmute
  Mute
